// Logisim project ELYTRA_COMPUTER_FINALE.circ as structural Verilog: 17 circuits, main circuit main
module main (
  input  in_1
);

  wire alu_1_cout, alu_1_z, and_1_out, clk_operator_1_clk_out, clock_1_out, clock_2_out, data_memory_1_clko,
       flag_control_1_condition_control, not_1_out, one_pulse_out, rgb_video_1_p1, rgb_video_1_p2,
       rgb_video_1_p3, rgb_video_2_p1, rgb_video_2_p2, rgb_video_2_p3, rgb_video_3_p1, rgb_video_3_p2,
       rgb_video_3_p3, rgb_video_4_p3, rgb_video_4_p5, start_stop_out;
  wire [0:0] control_rom_1_controls_3;
  wire [1:0] control_rom_1_controls_2, or_1_out;
  wire [2:0] control_rom_1_controls_4;
  wire [3:0] instruction_memory_1_instruction_2, instruction_memory_1_instruction_3, multiplexer_2_out,
       multiplexer_4_out, rgb_video_3_p4, rgb_video_3_p5;
  wire [5:0] rgb_video_2_p4, rgb_video_2_p5;
  wire [7:0] alu_1_result, data_memory_1_mainout, instruction_memory_1_instruction, multiplexer_3_out,
       multiplexer_5_out, register_file_1_r1_value, register_file_1_r2_value, rgb_video_1_p4, rgb_video_1_p5,
       rgb_video_2_p6, rgb_video_3_p6, rgb_video_4_p7;
  wire [9:0] adder_1_out, call_stack_1_out_5, multiplexer_1_out, program_counter_1_out_3;
  wire [15:0] control_rom_1_controls;
  wire [17:0] data_memory_1_vga256_16;
  wire [23:0] rgb_video_1_p6;
  wire [25:0] data_memory_1_vga256;
  wire [41:0] data_memory_1_rgb888;

  CALL_STACK call_stack_1 (
    .PUSH(control_rom_1_controls[12]), .POP(or_1_out[1]), .CLK(clk_operator_1_clk_out),
    .PC_PLUS_1(adder_1_out), .out_5(call_stack_1_out_5));
  Multiplexer #(.select(2), .width(10)) multiplexer_1 (
    .in0(adder_1_out), .in1({instruction_memory_1_instruction_2[1:0], instruction_memory_1_instruction}),
    .in2(call_stack_1_out_5), .in3(call_stack_1_out_5), .out(multiplexer_1_out), .sel(or_1_out));
  or or_1 (or_1_out[0], control_rom_1_controls[4], and_1_out);
  and and_1 (and_1_out, control_rom_1_controls[3], flag_control_1_condition_control);
  Adder #(.width(10)) adder_1 (
    .a(program_counter_1_out_3), .b({10{1'b0}}), .out(adder_1_out), .cin(1'b1));  // open: cout
  PROGRAM_COUNTER program_counter_1 (.in_1(multiplexer_1_out), .CLK(not_1_out), .out_3(program_counter_1_out_3));
  not not_1 (not_1_out, clk_operator_1_clk_out);
  // Probe on program_counter_1_out_3
  Clock clock_1 (.out(clock_1_out));
  // Probe on {instruction_memory_1_instruction_3, instruction_memory_1_instruction_2, instruction_memory_1_instruction}
  CLK_OPERATOR clk_operator_1 (
    .START_STOP(start_stop_out), .CLK(clock_1_out), .MANUAL(in_1), .ONE_PULSE(one_pulse_out),
    .HLT(control_rom_1_controls[0]), .CLK_OUT(clk_operator_1_clk_out));
  LED led_1 (.in(control_rom_1_controls[0]));
  Button start_stop (.out(start_stop_out));
  Button one_pulse (.out(one_pulse_out));
  INSTRUCTION_MEMORY instruction_memory_1 (
    .INSTRUCTION_ADDRESS(program_counter_1_out_3),
    .INSTRUCTION({instruction_memory_1_instruction_3, instruction_memory_1_instruction_2, instruction_memory_1_instruction}));
  Multiplexer #(.width(4)) multiplexer_2 (
    .in0(instruction_memory_1_instruction[3:0]), .in1(instruction_memory_1_instruction_2),
    .out(multiplexer_2_out), .sel(control_rom_1_controls[5]));
  Multiplexer #(.select(2), .width(8)) multiplexer_3 (
    .in0(alu_1_result), .in1(instruction_memory_1_instruction), .in2(data_memory_1_mainout),
    .in3(data_memory_1_mainout), .out(multiplexer_3_out), .sel(control_rom_1_controls_2));
  Multiplexer #(.width(4)) multiplexer_4 (
    .in0(instruction_memory_1_instruction[7:4]), .in1(instruction_memory_1_instruction[3:0]),
    .out(multiplexer_4_out), .sel(control_rom_1_controls_2[1]));
  CONTROL_ROM control_rom_1 (
    .OPCODE(instruction_memory_1_instruction_3),
    .CONTROLS({control_rom_1_controls[15:14], or_1_out[1], control_rom_1_controls[12], control_rom_1_controls_4, control_rom_1_controls[8], control_rom_1_controls_2[0], control_rom_1_controls_3[0], control_rom_1_controls[5:2], control_rom_1_controls_2[1], control_rom_1_controls[0]}));
  REGISTER_FILE register_file_1 (
    .WE(control_rom_1_controls[8]), .W(multiplexer_2_out), .CLK(clk_operator_1_clk_out),
    .R2(multiplexer_4_out), .R1(instruction_memory_1_instruction_2), .DATA(multiplexer_3_out),
    .R2_value(register_file_1_r2_value), .R1_value(register_file_1_r1_value));  // open: SET, RESET
  Multiplexer #(.select(2), .width(8)) multiplexer_5 (
    .in0(register_file_1_r2_value), .in1(instruction_memory_1_instruction),
    .in2({{5{instruction_memory_1_instruction[7]}}, instruction_memory_1_instruction[6:4]}),
    .in3({{5{instruction_memory_1_instruction[7]}}, instruction_memory_1_instruction[6:4]}),
    .out(multiplexer_5_out), .sel({control_rom_1_controls_2[1], control_rom_1_controls_3[0]}));
  ALU alu_1 (
    .A(register_file_1_r1_value), .B(multiplexer_5_out), .SETTING(control_rom_1_controls_4),
    .RESULT(alu_1_result), .Cout(alu_1_cout), .Z(alu_1_z));  // open: V, N
  // Probe on alu_1_result
  FLAG_CONTROL flag_control_1 (
    .FLAG_ENABLE(control_rom_1_controls[2]), .CLK(clk_operator_1_clk_out), .Cout(alu_1_cout), .ZERO(alu_1_z),
    .COND_setting(instruction_memory_1_instruction_2[3:2]),
    .CONDITION_CONTROL(flag_control_1_condition_control));
  DATA_MEMORY data_memory_1 (
    .EN(control_rom_1_controls_2[1]), .WE(control_rom_1_controls[14]), .CLK(clk_operator_1_clk_out),
    .DATA(register_file_1_r2_value), .ADDRESS(alu_1_result), .clko(data_memory_1_clko),
    .RGB888(data_memory_1_rgb888), .MAINOUT(data_memory_1_mainout), .VGA256(data_memory_1_vga256),
    .VGA256_16(data_memory_1_vga256_16));
  // RGB_Video #(.cursor("No Cursor"), .height(256), .reset("Synchronous"), .scale(1), .width(256)) rgb_video_1: pin names not known; wires that end beside it: rgb_video_1_p1, rgb_video_1_p2, rgb_video_1_p3, rgb_video_1_p4, rgb_video_1_p5, rgb_video_1_p6
  RGB_SCREEN_MANAGER rgb_screen_manager_1 (
    .clk(data_memory_1_clko), .SCREEN_CONTROL_SIGNAL(data_memory_1_rgb888), .clko(rgb_video_1_p2),
    .COLOUR_R8G8B8(rgb_video_1_p6), .RESET(rgb_video_1_p1), .SCREEN_WE(rgb_video_1_p3),
    .X_CORDS(rgb_video_1_p4), .Y_CORDS(rgb_video_1_p5));
  // RGB_Video #(.cursor("No Cursor"), .height(64), .reset("Synchronous"), .scale(4), .width(64)) rgb_video_2: pin names not known; wires that end beside it: rgb_video_2_p1, rgb_video_2_p2, rgb_video_2_p3, rgb_video_2_p4, rgb_video_2_p5, rgb_video_2_p6
  VGASCREENCONTROLS vgascreencontrols_1 (
    .in_1(data_memory_1_vga256), .CLK({data_memory_1_clko, rgb_video_2_p2}), .COLOUR_R8G8B8(rgb_video_2_p6),
    .RESET(rgb_video_2_p1), .SCREEN_WE(rgb_video_2_p3), .X_CORDS(rgb_video_2_p4), .Y_CORDS(rgb_video_2_p5));
  // RGB_Video #(.cursor("No Cursor"), .height(16), .reset("Synchronous"), .scale(8), .width(16)) rgb_video_3: pin names not known; wires that end beside it: rgb_video_3_p1, rgb_video_3_p2, rgb_video_3_p3, rgb_video_3_p4, rgb_video_3_p5, rgb_video_3_p6
  VGA256_16_CONTROLS vga256_16_controls_1 (
    .in_1(data_memory_1_vga256_16), .CLK({data_memory_1_clko, rgb_video_3_p2}),
    .COLOUR_R8G8B8(rgb_video_3_p6), .RESET(rgb_video_3_p1), .SCREEN_WE(rgb_video_3_p3),
    .X_CORDS(rgb_video_3_p4), .Y_CORDS(rgb_video_3_p5));
  Clock clock_2 (.out(clock_2_out));
  // RGB_Video #(.cursor("No Cursor"), .height(16), .reset("Synchronous"), .scale(8), .width(16)) rgb_video_4: pin names not known; wires that end beside it: clock_2_out, 1'b1, rgb_video_4_p3, rgb_video_4_p3, rgb_video_4_p5, rgb_video_4_p5, rgb_video_4_p7
  Slider slider_1 (.out(rgb_video_4_p7));
  Joystick joystick_1 ();  // open: x, y

  // Notes on the sheet:
  //   IMMIDIATE ACESS MUX
  //   RGB 888 256*256
  //   VGA256 64*64
  //   VGA256 16*16
  //   joystick
  //   FUNZONE
  //   color
  //   \/
endmodule

module ALU (
  input  [7:0] A,
  input  [7:0] B,
  input  [2:0] SETTING,
  output V,
  output Cout,
  output Z,
  output N,
  output [7:0] RESULT
);

  wire adder_1_cout, adder_2_cout, and_2_out, and_3_out, not_3_out, or_2_out, xor_2_out, xor_3_out;
  wire [7:0] adder_1_out, adder_2_out, and_1_out, bareel_shift_1_shifted_a, bareel_shift_2_shifted_a,
       not_1_out, not_2_out, or_1_out, xor_1_out;

  // Probe on A
  // Probe on B
  assign not_1_out = ~B;  // NOT_Gate not_1, 8 bits wide
  Adder adder_1 (.a(A), .b(B), .out(adder_1_out), .cin(1'b0), .cout(adder_1_cout));
  Adder adder_2 (.a(A), .b(not_1_out), .out(adder_2_out), .cin(1'b1), .cout(adder_2_cout));
  assign and_1_out = A & B;  // AND_Gate and_1, 8 bits wide
  assign or_1_out = A | B;  // OR_Gate or_1, 8 bits wide
  assign xor_1_out = A ^ B;  // XOR_Gate xor_1, 8 bits wide
  assign not_2_out = ~A;  // NOT_Gate not_2, 8 bits wide
  BAREEL_SHIFT bareel_shift_1 (.A(A), .B(B), .MODE(1'b1), .SHIFTED_A(bareel_shift_1_shifted_a));
  BAREEL_SHIFT bareel_shift_2 (.A(A), .B(B), .MODE(1'b0), .SHIFTED_A(bareel_shift_2_shifted_a));
  Multiplexer #(.select(3)) multiplexer_1 (
    .in0(adder_1_cout), .in1(adder_2_cout), .in2(1'b0), .in3(1'b0), .in4(1'b0), .in5(1'b0), .in6(1'b0),
    .in7(1'b0), .out(Cout), .sel(SETTING));
  Multiplexer #(.select(3), .width(8)) multiplexer_2 (
    .in0(adder_1_out), .in1(adder_2_out), .in2(and_1_out), .in3(or_1_out), .in4(xor_1_out), .in5(not_2_out),
    .in6(bareel_shift_1_shifted_a), .in7(bareel_shift_2_shifted_a), .out({N, RESULT[6:0]}), .sel(SETTING));
  not not_3 (not_3_out, xor_2_out);
  xor xor_2 (xor_2_out, A[7], B[7]);
  xor xor_3 (xor_3_out, A[7], N);
  and and_2 (and_2_out, not_3_out, xor_3_out);
  and and_3 (and_3_out, xor_2_out, xor_3_out);
  Multiplexer #(.select(3)) multiplexer_3 (
    .in0(and_2_out), .in1(and_3_out), .in2(1'b0), .in3(1'b0), .in4(1'b0), .in5(1'b0), .in6(1'b0), .in7(1'b0),
    .out(V), .sel(SETTING));
  or or_2 (or_2_out, RESULT[0], RESULT[1], RESULT[2], RESULT[3], RESULT[4], RESULT[5], RESULT[6], N);
  not not_4 (Z, or_2_out);
  // Probe on {N, RESULT[6:0]}

  assign RESULT[7] = N;

  // Notes on the sheet:
  //   ALU
endmodule

module REGISTER_FILE (
  input  WE,
  input  [3:0] W,
  input  CLK,
  input  [7:0] DATA,
  input  SET,
  input  RESET,
  input  [3:0] R1,
  input  [3:0] R2,
  output [7:0] R1_value,
  output [7:0] R2_value
);

  wire decoder_1_out1, decoder_1_out2, decoder_1_out3, decoder_1_out4, decoder_1_out5, decoder_1_out6,
       decoder_1_out7, decoder_1_out8, decoder_1_out9, decoder_1_out10, decoder_1_out11, decoder_1_out12,
       decoder_1_out13, decoder_1_out14, decoder_1_out15;
  wire [3:0] multiplexer_3_out;
  wire [7:0] e8_bit_register_1_o, e8_bit_register_2_o, e8_bit_register_3_o, e8_bit_register_4_o,
       e8_bit_register_5_o, e8_bit_register_6_o, e8_bit_register_7_o, e8_bit_register_8_o,
       e8_bit_register_9_o, e8_bit_register_10_o, e8_bit_register_11_o, e8_bit_register_12_o,
       e8_bit_register_13_o, e8_bit_register_14_o, e8_bit_register_15_o;

  Multiplexer #(.select(4), .width(8)) multiplexer_1 (
    .in0({8{1'b0}}), .in1(e8_bit_register_1_o), .in2(e8_bit_register_2_o), .in3(e8_bit_register_3_o),
    .in4(e8_bit_register_4_o), .in5(e8_bit_register_5_o), .in6(e8_bit_register_6_o),
    .in7(e8_bit_register_7_o), .in8(e8_bit_register_8_o), .in9(e8_bit_register_9_o),
    .in10(e8_bit_register_10_o), .in11(e8_bit_register_11_o), .in12(e8_bit_register_12_o),
    .in13(e8_bit_register_13_o), .in14(e8_bit_register_14_o), .in15(e8_bit_register_15_o), .out(R1_value),
    .sel(R1));
  Multiplexer #(.select(4), .width(8)) multiplexer_2 (
    .in0({8{1'b0}}), .in1(e8_bit_register_1_o), .in2(e8_bit_register_2_o), .in3(e8_bit_register_3_o),
    .in4(e8_bit_register_4_o), .in5(e8_bit_register_5_o), .in6(e8_bit_register_6_o),
    .in7(e8_bit_register_7_o), .in8(e8_bit_register_8_o), .in9(e8_bit_register_9_o),
    .in10(e8_bit_register_10_o), .in11(e8_bit_register_11_o), .in12(e8_bit_register_12_o),
    .in13(e8_bit_register_13_o), .in14(e8_bit_register_14_o), .in15(e8_bit_register_15_o), .out(R2_value),
    .sel(R2));
  Multiplexer #(.width(4)) multiplexer_3 (.in0(4'b0000), .in1(W), .out(multiplexer_3_out), .sel(CLK));
  E8_bit_register e8_bit_register_1 (.A(DATA), .CLK(decoder_1_out1), .SET(SET), .RESET(RESET), .O(e8_bit_register_1_o));
  E8_bit_register e8_bit_register_2 (.A(DATA), .CLK(decoder_1_out2), .SET(SET), .RESET(RESET), .O(e8_bit_register_2_o));
  // Probe on e8_bit_register_1_o
  // Probe on e8_bit_register_2_o
  Decoder #(.select(4)) decoder_1 (
    .out1(decoder_1_out1), .out2(decoder_1_out2), .out3(decoder_1_out3), .out4(decoder_1_out4),
    .out5(decoder_1_out5), .out6(decoder_1_out6), .out7(decoder_1_out7), .out8(decoder_1_out8),
    .out9(decoder_1_out9), .out10(decoder_1_out10), .out11(decoder_1_out11), .out12(decoder_1_out12),
    .out13(decoder_1_out13), .out14(decoder_1_out14), .out15(decoder_1_out15), .sel(multiplexer_3_out),
    .en(WE));  // open: out0
  E8_bit_register e8_bit_register_3 (.A(DATA), .CLK(decoder_1_out3), .SET(SET), .RESET(RESET), .O(e8_bit_register_3_o));
  // Probe on e8_bit_register_3_o
  E8_bit_register e8_bit_register_4 (.A(DATA), .CLK(decoder_1_out4), .SET(SET), .RESET(RESET), .O(e8_bit_register_4_o));
  // Probe on e8_bit_register_4_o
  E8_bit_register e8_bit_register_5 (.A(DATA), .CLK(decoder_1_out5), .SET(SET), .RESET(RESET), .O(e8_bit_register_5_o));
  E8_bit_register e8_bit_register_6 (.A(DATA), .CLK(decoder_1_out6), .SET(SET), .RESET(RESET), .O(e8_bit_register_6_o));
  // Probe on e8_bit_register_5_o
  // Probe on e8_bit_register_6_o
  E8_bit_register e8_bit_register_7 (.A(DATA), .CLK(decoder_1_out7), .SET(SET), .RESET(RESET), .O(e8_bit_register_7_o));
  // Probe on e8_bit_register_7_o
  E8_bit_register e8_bit_register_8 (.A(DATA), .CLK(decoder_1_out8), .SET(SET), .RESET(RESET), .O(e8_bit_register_8_o));
  // Probe on e8_bit_register_8_o
  E8_bit_register e8_bit_register_9 (.A(DATA), .CLK(decoder_1_out9), .SET(SET), .RESET(RESET), .O(e8_bit_register_9_o));
  E8_bit_register e8_bit_register_10 (
    .A(DATA), .CLK(decoder_1_out10), .SET(SET), .RESET(RESET), .O(e8_bit_register_10_o));
  // Probe on e8_bit_register_9_o
  // Probe on e8_bit_register_10_o
  E8_bit_register e8_bit_register_11 (
    .A(DATA), .CLK(decoder_1_out11), .SET(SET), .RESET(RESET), .O(e8_bit_register_11_o));
  // Probe on e8_bit_register_11_o
  E8_bit_register e8_bit_register_12 (
    .A(DATA), .CLK(decoder_1_out12), .SET(SET), .RESET(RESET), .O(e8_bit_register_12_o));
  // Probe on e8_bit_register_12_o
  E8_bit_register e8_bit_register_13 (
    .A(DATA), .CLK(decoder_1_out13), .SET(SET), .RESET(RESET), .O(e8_bit_register_13_o));
  E8_bit_register e8_bit_register_14 (
    .A(DATA), .CLK(decoder_1_out14), .SET(SET), .RESET(RESET), .O(e8_bit_register_14_o));
  // Probe on e8_bit_register_13_o
  // Probe on e8_bit_register_14_o
  E8_bit_register e8_bit_register_15 (
    .A(DATA), .CLK(decoder_1_out15), .SET(SET), .RESET(RESET), .O(e8_bit_register_15_o));
  // Probe on e8_bit_register_15_o

  // Notes on the sheet:
  //   R0
endmodule

module INSTRUCTION_MEMORY (
  input  [9:0] INSTRUCTION_ADDRESS,
  output [15:0] INSTRUCTION
);

  ROM #(.addrWidth(10), .dataWidth(16)) rom_1 (.addr(INSTRUCTION_ADDRESS), .data(INSTRUCTION));

  // Notes on the sheet:
  //   contents of rom_1 (hex, n*v repeats v):
  //   8114 820a 8301 8401 850f 8600 8704 8800 8a3f 8b01 8cff 8ffc ff11 ff02 fff5 ff37 ff38 210d 220e 2131
  //   2242 3100 b01a 31a0 b01c a01d 2b03 a01d 2c03 3200 b022 32a0 b024 a025 2b04 a025 2c04 ff11 ff02 fff5
  //   ff37 ff38 ff1d ff0e fff6 ff37 ff38 a011
endmodule

module CONTROL_ROM (
  input  [3:0] OPCODE,
  output [15:0] CONTROLS
);

  ROM #(.addrWidth(4), .dataWidth(16)) rom_1 (.addr(OPCODE), .data(CONTROLS));

  // Notes on the sheet:
  //   contents of rom_1 (hex, n*v repeats v):
  //   0 1 104 304 504 904 d04 f04 1a0 164 10 8 1010 2000 102 4002
endmodule

module PROGRAM_COUNTER (
  input  [9:0] in_1,
  input  CLK,
  output [9:0] out_3
);

  D_Flip_Flop d_ff_1 (.D(in_1[0]), .clk(CLK), .Q(out_3[0]));  // open: Qn, preset, reset
  D_Flip_Flop d_ff_2 (.D(in_1[1]), .clk(CLK), .Q(out_3[1]));  // open: Qn, preset, reset
  D_Flip_Flop d_ff_3 (.D(in_1[2]), .clk(CLK), .Q(out_3[2]));  // open: Qn, preset, reset
  D_Flip_Flop d_ff_4 (.D(in_1[3]), .clk(CLK), .Q(out_3[3]));  // open: Qn, preset, reset
  D_Flip_Flop d_ff_5 (.D(in_1[4]), .clk(CLK), .Q(out_3[4]));  // open: Qn, preset, reset
  D_Flip_Flop d_ff_6 (.D(in_1[5]), .clk(CLK), .Q(out_3[5]));  // open: Qn, preset, reset
  D_Flip_Flop d_ff_7 (.D(in_1[6]), .clk(CLK), .Q(out_3[6]));  // open: Qn, preset, reset
  D_Flip_Flop d_ff_8 (.D(in_1[7]), .clk(CLK), .Q(out_3[7]));  // open: Qn, preset, reset
  D_Flip_Flop d_ff_9 (.D(in_1[8]), .clk(CLK), .Q(out_3[8]));  // open: Qn, preset, reset
  D_Flip_Flop d_ff_10 (.D(in_1[9]), .clk(CLK), .Q(out_3[9]));  // open: Qn, preset, reset
endmodule

module CALL_STACK (
  input  PUSH,
  input  POP,
  input  [9:0] PC_PLUS_1,
  input  CLK,
  output [9:0] out_5
);

  wire or_1_out;
  wire [3:0] adder_1_out, counter_1_q, multiplexer_1_out;

  Counter #(.max('hf), .width(4)) counter_1 (
    .up(PUSH), .count(or_1_out), .clk(CLK), .Q(counter_1_q));  // open: clr, load, D, carry
  or or_1 (or_1_out, PUSH, POP);
  Adder #(.width(4)) adder_1 (.a(counter_1_q), .b(4'b1111), .out(adder_1_out));  // open: cin, cout
  RAM #(.addrWidth(4), .dataWidth(10)) ram_1 (
    .addr(multiplexer_1_out), .we(PUSH), .oe(1'b1), .clk(CLK), .din(PC_PLUS_1), .dout(out_5));
  Multiplexer #(.width(4)) multiplexer_1 (.in0(counter_1_q), .in1(adder_1_out), .out(multiplexer_1_out), .sel(POP));
endmodule

module DATA_MEMORY (
  input  [7:0] ADDRESS,
  input  [7:0] DATA,
  input  WE,
  input  EN,
  input  CLK,
  output [7:0] MAINOUT,
  output clko,
  output [41:0] RGB888,
  output [25:0] VGA256,
  output [17:0] VGA256_16
);

  wire and_1_out, and_2_out, M_248_out, M_249_out, M_250_out, M_251_out, M_252_out, M_253_out, M_254_out,
       M_255_out, not_1_out, not_2_out, not_3_out, not_4_out, not_5_out, not_6_out, not_7_out, not_8_out,
       not_9_out, not_10_out, not_11_out, not_12_out;
  wire [7:0] e8_bit_register_2_o, e8_bit_register_8_o;
  wire [7:4] e8_bit_register_1_o;

  and and_1 (and_1_out, WE, EN);
  and and_2 (and_2_out, CLK, and_1_out);
  not not_1 (not_1_out, ADDRESS[0]);
  not not_2 (not_2_out, ADDRESS[1]);
  not not_3 (not_3_out, ADDRESS[0]);
  not not_4 (not_4_out, ADDRESS[1]);
  not not_5 (not_5_out, ADDRESS[2]);
  not not_6 (not_6_out, ADDRESS[0]);
  not not_7 (not_7_out, ADDRESS[2]);
  not not_8 (not_8_out, ADDRESS[1]);
  not not_9 (not_9_out, ADDRESS[2]);
  not not_10 (not_10_out, ADDRESS[0]);
  not not_11 (not_11_out, ADDRESS[1]);
  not not_12 (not_12_out, ADDRESS[2]);
  and M_255 (M_255_out, ADDRESS[0], ADDRESS[1], ADDRESS[2], ADDRESS[3], ADDRESS[4], ADDRESS[5], ADDRESS[6], ADDRESS[7], and_2_out);
  and M_254 (M_254_out, not_1_out, ADDRESS[1], ADDRESS[2], ADDRESS[3], ADDRESS[4], ADDRESS[5], ADDRESS[6], ADDRESS[7], and_2_out);
  and M_253 (M_253_out, ADDRESS[0], not_2_out, ADDRESS[2], ADDRESS[3], ADDRESS[4], ADDRESS[5], ADDRESS[6], ADDRESS[7], and_2_out);
  and M_252 (M_252_out, not_3_out, not_4_out, ADDRESS[2], ADDRESS[3], ADDRESS[4], ADDRESS[5], ADDRESS[6], ADDRESS[7], and_2_out);
  and M_251 (M_251_out, ADDRESS[0], ADDRESS[1], not_5_out, ADDRESS[3], ADDRESS[4], ADDRESS[5], ADDRESS[6], ADDRESS[7], and_2_out);
  and M_250 (M_250_out, not_6_out, ADDRESS[1], not_7_out, ADDRESS[3], ADDRESS[4], ADDRESS[5], ADDRESS[6], ADDRESS[7], and_2_out);
  and M_249 (M_249_out, ADDRESS[0], not_8_out, not_9_out, ADDRESS[3], ADDRESS[4], ADDRESS[5], ADDRESS[6], ADDRESS[7], and_2_out);
  and M_248 (M_248_out, not_10_out, not_11_out, not_12_out, ADDRESS[3], ADDRESS[4], ADDRESS[5], ADDRESS[6], ADDRESS[7], and_2_out);
  RAM #(.enables("line")) ram_1 (.addr(ADDRESS), .we(and_1_out), .clk(CLK), .din(DATA), .dout(MAINOUT));
  E8_bit_register e8_bit_register_1 (
    .A(DATA), .CLK(M_255_out), .O({e8_bit_register_1_o, VGA256_16[1], VGA256[1], RGB888[1:0]}));  // open: SET, RESET
  E8_bit_register e8_bit_register_2 (.A(DATA), .CLK(M_254_out), .O(e8_bit_register_2_o));  // open: SET, RESET
  E8_bit_register e8_bit_register_3 (.A(DATA), .CLK(M_253_out), .O(RGB888[9:2]));  // open: SET, RESET
  E8_bit_register e8_bit_register_4 (.A(DATA), .CLK(M_252_out), .O(RGB888[17:10]));  // open: SET, RESET
  E8_bit_register e8_bit_register_5 (.A(DATA), .CLK(M_251_out), .O(RGB888[25:18]));  // open: SET, RESET
  E8_bit_register e8_bit_register_6 (.A(DATA), .CLK(M_250_out), .O(RGB888[33:26]));  // open: SET, RESET
  E8_bit_register e8_bit_register_7 (.A(DATA), .CLK(M_249_out), .O(RGB888[41:34]));  // open: SET, RESET
  E8_bit_register e8_bit_register_8 (.A(DATA), .CLK(M_248_out), .O(e8_bit_register_8_o));  // open: SET, RESET
  // Probe on MAINOUT

  assign clko = CLK;
  assign {VGA256[25:2], VGA256[0]} = {RGB888[25:2], RGB888[0]};
  assign {VGA256_16[17:2], VGA256_16[0]} = {RGB888[17:2], RGB888[0]};

  // Notes on the sheet:
  //   XCORDS
  //   YCORDS
  //   VGA 256 332
  //   16*16
  //   XCORDS
  //   YCORDS
  //   VGA 256 332
  //   64*64
  //   RGB SCREEN
  //   256*256
  //   OUTPUT CONTROLS
  //   INPUT CONTROL
  //   XCORDS
  //   YCORDS
  //   RED
  //   GREEN
  //   BLUE
endmodule

module FLAG_CONTROL (
  input  ZERO,
  input  Cout,
  input  CLK,
  input  [1:0] COND_setting,
  input  FLAG_ENABLE,
  output CONDITION_CONTROL
);

  wire and_1_out, d_ff_1_q, d_ff_1_qn, d_ff_2_q, d_ff_2_qn;

  and and_1 (and_1_out, CLK, FLAG_ENABLE);
  D_Flip_Flop d_ff_1 (.D(ZERO), .clk(and_1_out), .Q(d_ff_1_q), .Qn(d_ff_1_qn));  // open: preset, reset
  D_Flip_Flop d_ff_2 (.D(Cout), .clk(and_1_out), .Q(d_ff_2_q), .Qn(d_ff_2_qn));  // open: preset, reset
  Multiplexer #(.select(2)) multiplexer_1 (
    .in0(d_ff_1_q), .in1(d_ff_1_qn), .in2(d_ff_2_q), .in3(d_ff_2_qn), .out(CONDITION_CONTROL),
    .sel(COND_setting));
endmodule

module BAREEL_SHIFT (
  input  [7:0] A,
  input  [7:0] B,
  input  MODE,
  output [7:0] SHIFTED_A
);

  wire or_1_out;
  wire [7:0] multiplexer_1_out, multiplexer_2_out, multiplexer_3_out, one_shifter_1_b, one_shifter_2_b,
       one_shifter_3_b, one_shifter_4_b, one_shifter_5_b, one_shifter_6_b, one_shifter_7_b;

  ONE_SHIFTER one_shifter_1 (.A(A), .MODE(MODE), .B(one_shifter_1_b));
  Multiplexer #(.width(8)) multiplexer_1 (.in0(A), .in1(one_shifter_1_b), .out(multiplexer_1_out), .sel(B[0]));
  ONE_SHIFTER one_shifter_2 (.A(multiplexer_1_out), .MODE(MODE), .B(one_shifter_2_b));
  Multiplexer #(.width(8)) multiplexer_2 (
    .in0(multiplexer_1_out), .in1(one_shifter_3_b), .out(multiplexer_2_out), .sel(B[1]));
  ONE_SHIFTER one_shifter_3 (.A(one_shifter_2_b), .MODE(MODE), .B(one_shifter_3_b));
  ONE_SHIFTER one_shifter_4 (.A(multiplexer_2_out), .MODE(MODE), .B(one_shifter_4_b));
  ONE_SHIFTER one_shifter_5 (.A(one_shifter_4_b), .MODE(MODE), .B(one_shifter_5_b));
  ONE_SHIFTER one_shifter_6 (.A(one_shifter_5_b), .MODE(MODE), .B(one_shifter_6_b));
  ONE_SHIFTER one_shifter_7 (.A(one_shifter_6_b), .MODE(MODE), .B(one_shifter_7_b));
  Multiplexer #(.width(8)) multiplexer_3 (
    .in0(multiplexer_2_out), .in1(one_shifter_7_b), .out(multiplexer_3_out), .sel(B[2]));
  Multiplexer #(.width(8)) multiplexer_4 (.in0(multiplexer_3_out), .in1({8{1'b0}}), .out(SHIFTED_A), .sel(or_1_out));
  or or_1 (or_1_out, B[3], B[4], B[5], B[6], B[7]);

  // Notes on the sheet:
  //   0 LSR
  //   1 LSL
endmodule

module ONE_SHIFTER (
  input  [7:0] A,
  input  MODE,
  output [7:0] B
);

  Multiplexer #(.width(8)) multiplexer_1 (.in0({1'b0, A[7:1]}), .in1({A[6:0], 1'b0}), .out(B), .sel(MODE));

  // Notes on the sheet:
  //   0 (right shift)
  //   1 (LEFT SHIFT)
endmodule

module E8_bit_register (
  input  [7:0] A,
  input  CLK,
  input  SET,
  input  RESET,
  output [7:0] O
);

  D_Flip_Flop d_ff_1 (.D(A[0]), .clk(CLK), .Q(O[0]), .preset(SET), .reset(RESET));  // open: Qn
  D_Flip_Flop d_ff_2 (.D(A[1]), .clk(CLK), .Q(O[1]), .preset(SET), .reset(RESET));  // open: Qn
  D_Flip_Flop d_ff_3 (.D(A[2]), .clk(CLK), .Q(O[2]), .preset(SET), .reset(RESET));  // open: Qn
  D_Flip_Flop d_ff_4 (.D(A[3]), .clk(CLK), .Q(O[3]), .preset(SET), .reset(RESET));  // open: Qn
  D_Flip_Flop d_ff_5 (.D(A[4]), .clk(CLK), .Q(O[4]), .preset(SET), .reset(RESET));  // open: Qn
  D_Flip_Flop d_ff_6 (.D(A[5]), .clk(CLK), .Q(O[5]), .preset(SET), .reset(RESET));  // open: Qn
  D_Flip_Flop d_ff_7 (.D(A[6]), .clk(CLK), .Q(O[6]), .preset(SET), .reset(RESET));  // open: Qn
  D_Flip_Flop d_ff_8 (.D(A[7]), .clk(CLK), .Q(O[7]), .preset(SET), .reset(RESET));  // open: Qn
endmodule

module E10_bit_register (
  input  [9:0] INP,
  input  CLK,
  output [9:0] OUTp
);

  D_Flip_Flop d_ff_1 (.D(INP[0]), .clk(CLK), .Q(OUTp[0]));  // open: Qn, preset, reset
  D_Flip_Flop d_ff_2 (.D(INP[1]), .clk(CLK), .Q(OUTp[1]));  // open: Qn, preset, reset
  D_Flip_Flop d_ff_3 (.D(INP[2]), .clk(CLK), .Q(OUTp[2]));  // open: Qn, preset, reset
  D_Flip_Flop d_ff_4 (.D(INP[3]), .clk(CLK), .Q(OUTp[3]));  // open: Qn, preset, reset
  D_Flip_Flop d_ff_5 (.D(INP[4]), .clk(CLK), .Q(OUTp[4]));  // open: Qn, preset, reset
  D_Flip_Flop d_ff_6 (.D(INP[5]), .clk(CLK), .Q(OUTp[5]));  // open: Qn, preset, reset
  D_Flip_Flop d_ff_7 (.D(INP[6]), .clk(CLK), .Q(OUTp[6]));  // open: Qn, preset, reset
  D_Flip_Flop d_ff_8 (.D(INP[7]), .clk(CLK), .Q(OUTp[7]));  // open: Qn, preset, reset
  D_Flip_Flop d_ff_9 (.D(INP[8]), .clk(CLK), .Q(OUTp[8]));  // open: Qn, preset, reset
  D_Flip_Flop d_ff_10 (.D(INP[9]), .clk(CLK), .Q(OUTp[9]));  // open: Qn, preset, reset
endmodule

module RGB_SCREEN_MANAGER (
  input  [41:0] SCREEN_CONTROL_SIGNAL,
  input  clk,
  output RESET,
  output SCREEN_WE,
  output [7:0] X_CORDS,
  output [7:0] Y_CORDS,
  output [23:0] COLOUR_R8G8B8,
  output clko
);

  not not_1 (clko, clk);

  assign COLOUR_R8G8B8 = SCREEN_CONTROL_SIGNAL[41:18];
  assign RESET = SCREEN_CONTROL_SIGNAL[0];
  assign SCREEN_WE = SCREEN_CONTROL_SIGNAL[1];
  assign X_CORDS = SCREEN_CONTROL_SIGNAL[9:2];
  assign Y_CORDS = SCREEN_CONTROL_SIGNAL[17:10];
endmodule

module CLK_OPERATOR (
  input  START_STOP,
  input  CLK,
  input  ONE_PULSE,
  input  MANUAL,
  input  HLT,
  output CLK_OUT
);

  wire d_ff_1_q, multiplexer_1_out, multiplexer_2_out, t_ff_1_q;

  T_Flip_Flop t_ff_1 (.T(1'b1), .clk(START_STOP), .Q(t_ff_1_q));  // open: Qn, reset, preset
  Multiplexer multiplexer_1 (.in0(1'b0), .in1(CLK), .out(multiplexer_1_out), .sel(t_ff_1_q));
  Multiplexer multiplexer_2 (.in0(multiplexer_1_out), .in1(ONE_PULSE), .out(multiplexer_2_out), .sel(MANUAL));
  D_Flip_Flop d_ff_1 (.D(1'b1), .clk(HLT), .Q(d_ff_1_q));  // open: Qn, preset, reset
  Multiplexer multiplexer_3 (.in0(multiplexer_2_out), .in1(1'b0), .out(CLK_OUT), .sel(d_ff_1_q));
endmodule

module VGASCREENCONTROLS (
  input  [25:0] in_1,
  input  CLK,
  output RESET,
  output SCREEN_WE,
  output [5:0] X_CORDS,
  output [5:0] Y_CORDS,
  output [7:0] COLOUR_R8G8B8,
  output CLKO
);


  assign CLKO = CLK;
  assign COLOUR_R8G8B8 = in_1[25:18];
  assign RESET = in_1[0];
  assign SCREEN_WE = in_1[1];
  assign X_CORDS = in_1[7:2];
  assign Y_CORDS = in_1[15:10];
endmodule

module VGA256_16_CONTROLS (
  input  [17:0] in_1,
  input  CLK,
  output RESET,
  output SCREEN_WE,
  output [3:0] X_CORDS,
  output [3:0] Y_CORDS,
  output [7:0] COLOUR_R8G8B8,
  output CLKO
);


  assign CLKO = CLK;
  assign COLOUR_R8G8B8 = in_1[17:10];
  assign RESET = in_1[0];
  assign SCREEN_WE = in_1[1];
  assign X_CORDS = in_1[5:2];
  assign Y_CORDS = in_1[9:6];
endmodule
